// Digital circuit MMP-1.dig as structural Verilog
module MMP_1 (
  input  _4Hz,
  input  _100Hz,
  input  clk
);

  wire Addr_Dest, Addr_Src, Addr_Step, alu_1_data_ready, and_1_out, and_2_out, and_3_out, and_4_out,
       and_5_out, and_6_out, and_7_out, and_8_out, and_9_out, and_10_out, and_11_out, and_12_out, and_13_out,
       and_14_out, and_15_out, and_16_out, and_17_out, and_18_out, and_19_out, and_20_out, buttonled_1_p1,
       buttonled_1_p2, buttonled_2_p1, buttonled_2_p2, buttonled_3_p1, buttonled_3_p2, buttonled_4_p1,
       buttonled_4_p2, Clk_t, comparator_1_eq, comparator_2_eq, comparator_3_eq, comparator_3_gt,
       comparator_3_lt, comparator_4_lt, comparator_5_eq, comparator_6_eq, comparator_7_eq, comparator_8_eq,
       counter_1_ovf, demultiplexer_1_out_0, demultiplexer_1_out_1, demultiplexer_1_out_2,
       demultiplexer_1_out_3, nClk, not_1_out, not_2_out, not_3_out, not_4_out, nRst, or_1_out, or_2_out,
       Out_Dev, Res_out, rs_ff_as_2_q, rs_ff_as_3_q, rs_ff_as_4_nq, rs_ff_as_4_q, rs_ff_as_5_q, Rst,
       Step_2_out, Step_Inc;
  wire [1:0] clockselect_1_num, counter_1_out, counter_2_out, multiplexer_13_out;
  wire [4:0] MatrixXIndex_q;
  wire [10:0] Addr_Match_out;
  wire [15:0] Addr, Dest, multiplexer_2_out, multiplexer_3_out, multiplexer_13_out_3, PrgmStep, Src;
  wire [15:2] multiplexer_13_out_2;
  wire [31:0] alu_1_data_out, DispA, DispB, MatrixCValues_q, multiplexer_1_out, multiplexer_5_out,
       multiplexer_6_out, multiplexer_7_out, multiplexer_8_out, multiplexer_9_out, multiplexer_10_out,
       multiplexer_11_out, multiplexer_12_out, ramdualport_1_d, rom_1_d, Temp_q;

  Button Res (.out(Res_out));
  RS_FF_AS rs_ff_as_1 (.S(Res_out), .R(counter_1_ovf), .Q(Rst), .nQ(nRst));
  Register #(.Bits(32)) Temp (
    .D({multiplexer_13_out_3, multiplexer_13_out_2, multiplexer_13_out}), .C(Clk_t), .en(Addr_Src), .Q(Temp_q));
  Register #(.Bits(16)) u_Src (.D(multiplexer_13_out_3), .C(Clk_t), .en(Addr_Step), .Q(Src));
  Register #(.Bits(16)) u_Dest (.D({multiplexer_13_out_2, multiplexer_13_out}), .C(Clk_t), .en(Addr_Step), .Q(Dest));
  Comparator #(.Bits(16)) comparator_1 (.a(Dest), .b({16{1'b1}}), .eq(comparator_1_eq));  // open: gt, lt
  and and_1 (and_1_out, Addr_Dest, comparator_1_eq);
  CounterPreset #(.Bits(16)) Step (
    .en(and_2_out), .C(Clk_t), .dir(1'b0), .in({multiplexer_13_out_2, multiplexer_13_out}), .ld(and_1_out),
    .clr(Rst), .out(PrgmStep));  // open: ovf
  Multiplexer #(.Bits(32)) multiplexer_1 (.sel(Addr_Dest), .in_0({32{1'b0}}), .in_1(Temp_q), .out(multiplexer_1_out));
  and and_2 (and_2_out, Step_Inc, not_1_out);
  Counter #(.Bits(2)) counter_1 (.en(Rst), .C(nClk), .clr(nRst), .out(counter_1_out), .ovf(counter_1_ovf));
  Multiplexer #(.Bits(16)) multiplexer_2 (.sel(Addr_Src), .in_0({16{1'b0}}), .in_1(Src), .out(multiplexer_2_out));
  Multiplexer #(.Bits(16)) multiplexer_3 (
    .sel(Addr_Dest), .in_0(multiplexer_2_out), .in_1(Dest), .out(multiplexer_3_out));
  not not_1 (not_1_out, comparator_1_eq);
  Multiplexer #(.Bits(16)) multiplexer_4 (.sel(Addr_Step), .in_0(multiplexer_3_out), .in_1(PrgmStep), .out(Addr));
  not not_2 (not_2_out, Addr_Step);
  Button Step_2 (.out(Step_2_out));
  not not_3 (not_3_out, Step_2_out);
  RS_FF_AS rs_ff_as_2 (.S(not_3_out), .R(or_2_out), .Q(rs_ff_as_2_q));  // open: nQ
  RS_FF_AS rs_ff_as_3 (.S(not_2_out), .R(rs_ff_as_4_nq), .Q(rs_ff_as_3_q));  // open: nQ
  Comparator #(.Bits(16)) comparator_2 (.a(Addr), .b(16'hfff0), .eq(comparator_2_eq));  // open: gt, lt
  Comparator #(.Bits(16)) comparator_3 (
    .a(Addr), .b(16'h4000), .gt(comparator_3_gt), .eq(comparator_3_eq), .lt(comparator_3_lt));
  Comparator #(.Bits(16)) comparator_4 (.a(Addr), .b(16'h8000), .lt(comparator_4_lt));  // open: gt, eq
  // Probe Source on Src
  // Probe Destination on Dest
  and and_3 (and_3_out, Step_2_out, rs_ff_as_2_q);
  and and_4 (and_4_out, Addr_Step, rs_ff_as_3_q);
  RS_FF_AS rs_ff_as_4 (.S(and_3_out), .R(or_2_out), .Q(rs_ff_as_4_q), .nQ(rs_ff_as_4_nq));
  RS_FF_AS rs_ff_as_5 (.S(and_4_out), .R(rs_ff_as_4_nq), .Q(rs_ff_as_5_q));  // open: nQ
  and and_5 (and_5_out, Addr_Dest, comparator_2_eq);
  and and_6 (and_6_out, comparator_2_eq, Out_Dev);
  or or_1 (or_1_out, comparator_3_gt, comparator_3_eq);
  and and_7 (and_7_out, or_1_out, comparator_4_lt);
  or or_2 (or_2_out, rs_ff_as_5_q, not_4_out);
  // Probe Program Step on PrgmStep
  // Probe Address on Addr
  // Probe Bus on {multiplexer_13_out_3, multiplexer_13_out_2, multiplexer_13_out}
  // ButtonLED buttonled_1: pin names not known; wires that end beside it: buttonled_1_p1, buttonled_1_p2
  // ButtonLED buttonled_2: pin names not known; wires that end beside it: buttonled_2_p1, buttonled_2_p2
  // ButtonLED buttonled_3: pin names not known; wires that end beside it: buttonled_3_p1, buttonled_3_p2
  // ButtonLED buttonled_4: pin names not known; wires that end beside it: buttonled_4_p1, buttonled_4_p2
  and and_8 (and_8_out, clk, rs_ff_as_4_q);
  not not_4 (not_4_out, buttonled_2_p2);
  and and_9 (and_9_out, comparator_3_lt, Out_Dev);
  and and_10 (and_10_out, comparator_3_lt, Addr_Dest);
  and and_11 (and_11_out, Addr_Dest, and_7_out);
  and and_12 (and_12_out, and_7_out, Out_Dev);
  ClockSelect clockselect_1 (
    .ManA(buttonled_1_p1), .ManB(buttonled_2_p1), .ManC(buttonled_3_p1), .ManD(buttonled_4_p1),
    .ClkA(Step_2_out), .ClkB(and_8_out), .ClkC(_4Hz), .ClkD(_100Hz), .AutoA(demultiplexer_1_out_0),
    .AutoB(demultiplexer_1_out_1), .AutoC(demultiplexer_1_out_2), .AutoD(demultiplexer_1_out_3),
    .DispA(buttonled_1_p2), .DispB(buttonled_2_p2), .DispC(buttonled_3_p2), .DispD(buttonled_4_p2),
    .Clk(Clk_t), .nClk(nClk), .Num(clockselect_1_num));
  Demultiplexer #(.Selector_Bits(2)) demultiplexer_1 (
    .sel(multiplexer_13_out), .in(and_5_out), .out_0(demultiplexer_1_out_0), .out_1(demultiplexer_1_out_1),
    .out_2(demultiplexer_1_out_2), .out_3(demultiplexer_1_out_3));
  ROM #(.bigEndian("true"), .AddrBits(14), .Bits(32)) rom_1 (.A(Addr[13:0]), .sel(1'b1), .D(rom_1_d));
  LED ErrROMWrite (.in(and_10_out));
  RAMDualPort #(.AddrBits(14), .Bits(32)) ramdualport_1 (
    .A(Addr[13:0]), .Din({multiplexer_13_out_3, multiplexer_13_out_2, multiplexer_13_out}), .str(and_11_out),
    .C(Clk_t), .ld(1'b1), .D(ramdualport_1_d));
  // Probe on clockselect_1_num
  Multiplexer #(.Bits(32)) multiplexer_5 (
    .sel(and_6_out), .in_0(multiplexer_1_out), .in_1({{30{1'b0}}, clockselect_1_num}), .out(multiplexer_5_out));
  Multiplexer #(.Bits(32)) multiplexer_6 (
    .sel(and_9_out), .in_0(multiplexer_5_out), .in_1(rom_1_d), .out(multiplexer_6_out));
  Multiplexer #(.Bits(32)) multiplexer_7 (
    .sel(and_12_out), .in_0(multiplexer_6_out), .in_1(ramdualport_1_d), .out(multiplexer_7_out));
  Counter #(.Bits(2)) counter_2 (.en(1'b1), .C(nClk), .clr(Rst), .out(counter_2_out));  // open: ovf
  Decoder #(.Selector_Bits(2)) decoder_1 (
    .sel(counter_2_out), .out_0(Addr_Step), .out_1(Addr_Src), .out_2(Addr_Dest), .out_3(Step_Inc));
  Comparator #(.Bits(16)) comparator_5 (.a(Addr), .b(16'hf100), .eq(comparator_5_eq));  // open: gt, lt
  Comparator #(.Bits(16)) comparator_6 (.a(Addr), .b(16'hf101), .eq(comparator_6_eq));  // open: gt, lt
  Comparator #(.Bits(16)) comparator_7 (.a(Addr), .b(16'hf200), .eq(comparator_7_eq));  // open: gt, lt
  Comparator #(.Bits(16)) comparator_8 (.a(Addr), .b(16'hf201), .eq(comparator_8_eq));  // open: gt, lt
  LookUpTable #(.Bits(11)) Addr_Match (
    .in0(Addr[0]), .in1(Addr[1]), .in2(Addr[2]), .in3(Addr[3]), .in4(Addr[4]), .in5(Addr[5]), .in6(Addr[6]),
    .in7(Addr[7]), .in8(Addr[8]), .in9(Addr[9]), .in10(Addr[10]), .in11(Addr[11]), .in12(Addr[12]),
    .in13(Addr[13]), .in14(Addr[14]), .in15(Addr[15]), .out(Addr_Match_out));
  and and_13 (and_13_out, Addr_Dest, comparator_5_eq);
  and and_14 (and_14_out, comparator_5_eq, Out_Dev);
  and and_15 (and_15_out, Addr_Dest, comparator_6_eq);
  and and_16 (and_16_out, comparator_6_eq, Out_Dev);
  and and_17 (and_17_out, Addr_Dest, comparator_7_eq);
  and and_18 (and_18_out, comparator_7_eq, Out_Dev);
  and and_19 (and_19_out, Addr_Dest, comparator_8_eq);
  and and_20 (and_20_out, comparator_8_eq, Out_Dev);
  or or_3 (Out_Dev, Addr_Src, Addr_Step);
  Register #(.Bits(32)) u_DispA (
    .D({multiplexer_13_out_3, multiplexer_13_out_2, multiplexer_13_out}), .C(Clk_t), .en(and_13_out),
    .Q(DispA));
  Register #(.Bits(32)) u_DispB (
    .D({multiplexer_13_out_3, multiplexer_13_out_2, multiplexer_13_out}), .C(Clk_t), .en(and_15_out),
    .Q(DispB));
  Register #(.Bits(5)) MatrixXIndex (
    .D({multiplexer_13_out_2[4:2], multiplexer_13_out}), .C(Clk_t), .en(and_17_out), .Q(MatrixXIndex_q));
  Register #(.Bits(32)) MatrixCValues (
    .D({multiplexer_13_out_3, multiplexer_13_out_2, multiplexer_13_out}), .C(Clk_t), .en(and_19_out),
    .Q(MatrixCValues_q));
  ALU alu_1 (
    .Ctrl_In(Addr_Dest), .Ctrl_Out(Out_Dev), .Clk(Clk_t),
    .Data_In({multiplexer_13_out_3, multiplexer_13_out_2, multiplexer_13_out}), .Sel_A(Addr_Match_out[0]),
    .Sel_B(Addr_Match_out[1]), .Sel_SUM(Addr_Match_out[2]), .Sel_AND(Addr_Match_out[3]),
    .Sel_OR(Addr_Match_out[4]), .Sel_XOR(Addr_Match_out[5]), .Sel_NOT(Addr_Match_out[6]),
    .Sel_GT(Addr_Match_out[7]), .Sel_GTE(Addr_Match_out[8]), .Sel_LT(Addr_Match_out[9]),
    .Sel_LTE(Addr_Match_out[10]), .Data_Out(alu_1_data_out), .Data_Ready(alu_1_data_ready));
  LED led_1 (.in(Addr_Step));
  LED led_2 (.in(Addr_Src));
  LED led_3 (.in(Addr_Dest));
  LED led_4 (.in(Step_Inc));
  LedMatrix #(.colAddrBits(5), .rowDataBits(32)) ledmatrix_1 (.rows(MatrixCValues_q), .column(MatrixXIndex_q));
  Multiplexer #(.Bits(32)) multiplexer_8 (
    .sel(and_14_out), .in_0(multiplexer_7_out), .in_1(DispA), .out(multiplexer_8_out));
  Multiplexer #(.Bits(32)) multiplexer_9 (
    .sel(and_16_out), .in_0(multiplexer_8_out), .in_1(DispB), .out(multiplexer_9_out));
  Multiplexer #(.Bits(32)) multiplexer_10 (
    .sel(and_18_out), .in_0(multiplexer_9_out), .in_1({{27{1'b0}}, MatrixXIndex_q}), .out(multiplexer_10_out));
  Multiplexer #(.Bits(32)) multiplexer_11 (
    .sel(and_20_out), .in_0(multiplexer_10_out), .in_1(MatrixCValues_q), .out(multiplexer_11_out));
  Multiplexer #(.Bits(32)) multiplexer_12 (
    .sel(alu_1_data_ready), .in_0(multiplexer_11_out), .in_1(alu_1_data_out), .out(multiplexer_12_out));
  Multiplexer #(.Bits(32)) multiplexer_13 (
    .sel(Rst), .in_0(multiplexer_12_out), .in_1({32{1'b0}}),
    .out({multiplexer_13_out_3, multiplexer_13_out_2, multiplexer_13_out}));
  Seven_Seg_Hex seven_seg_hex_1 (.d(DispA[31:28]), .dp(1'b0));
  Seven_Seg_Hex seven_seg_hex_2 (.d(DispB[31:28]), .dp(1'b0));
  Seven_Seg_Hex seven_seg_hex_3 (.d(DispA[27:24]), .dp(1'b0));
  Seven_Seg_Hex seven_seg_hex_4 (.d(DispB[27:24]), .dp(1'b0));
  Seven_Seg_Hex seven_seg_hex_5 (.d(DispA[23:20]), .dp(1'b0));
  Seven_Seg_Hex seven_seg_hex_6 (.d(DispB[23:20]), .dp(1'b0));
  Seven_Seg_Hex seven_seg_hex_7 (.d(DispA[19:16]), .dp(1'b0));
  Seven_Seg_Hex seven_seg_hex_8 (.d(DispB[19:16]), .dp(1'b0));
  Seven_Seg_Hex seven_seg_hex_9 (.d(DispA[15:12]), .dp(1'b0));
  Seven_Seg_Hex seven_seg_hex_10 (.d(DispB[15:12]), .dp(1'b0));
  Seven_Seg_Hex seven_seg_hex_11 (.d(DispA[11:8]), .dp(1'b0));
  Seven_Seg_Hex seven_seg_hex_12 (.d(DispB[11:8]), .dp(1'b0));
  Seven_Seg_Hex seven_seg_hex_13 (.d(DispA[7:4]), .dp(1'b0));
  Seven_Seg_Hex seven_seg_hex_14 (.d(DispB[7:4]), .dp(1'b0));
  Seven_Seg_Hex seven_seg_hex_15 (.d(DispA[3:0]), .dp(1'b0));
  Seven_Seg_Hex seven_seg_hex_16 (.d(DispB[3:0]), .dp(1'b0));

  // Other names for the same wires on the sheet: MemAddr[13:0] = Addr[13:0]; In_Temp = Addr_Src;
  //   In_SrcDest = Addr_Step; NextInstr = Addr_Step; In_Dev = Addr_Dest; Out_Temp = Addr_Dest

  // Notes on the sheet:
  //   _4Hz: Hz: 4
  //   _100Hz: Hz: 100
  //   clk: Hz: 8
  //   0x0000-0x3FFF : ROM
  //   0x4000-0x7FFF : RAM
  //   0xF000-0xF00A : ALU A, B,
  //   SUM, AND, OR, XOR, NOT,
  //   GT, GTE, LT, LTE
  //   0xF100 : Display A
  //   0xF101 : Display B
  //   0xF200 : Matrix X index
  //   0xF201 : Matrix Column values
  //   0xFFF0 : Clock Select
  //   0xFFFF : Step
  //   Clock Generation
  //   ROM / RAM
  //   Single Clock
  //   Instruction
  //   4Hz
  //   100Hz
  //   rom_1 loads program.bin
  //   Control changes on -Clk
  //   Data changes on +Clk
  //   Hex Displays
  //   contents of Addr_Match (hex, n*v repeats v):
  //   61440*0,1,2,4,8,10,20,40,80,100,200,400
  //   Load pointers
  //   Read Source
  //   Write Destination
  //   Increment Step
endmodule
